// Logisim project ULA.circ as structural Verilog: 16 circuits, main circuit Subtrator Maior/Menor
module Subtrator_Maior_Menor (
  input  A3,
  input  A2,
  input  A1,
  input  A0,
  input  B3,
  input  B2,
  input  B1,
  input  B0,
  output out_9,
  output out_10,
  output out_11,
  output out_12
);

  wire subtratorc1_1_t_out, subtratorc2_1_t_out, subtratorc3_1_t_out, subtratorh_1_t_out;

  SubtratorH subtratorh_1 (.A(A0), .B(B0), .S(out_9), .T_out(subtratorh_1_t_out));
  SubtratorC3 subtratorc3_1 (.A(A1), .B(B1), .T_in(subtratorh_1_t_out), .S(out_10), .T_out(subtratorc3_1_t_out));
  SubtratorC2 subtratorc2_1 (.A(A2), .B(B2), .T_in(subtratorc3_1_t_out), .S(out_11), .T_out(subtratorc2_1_t_out));
  SubtratorC1 subtratorc1_1 (.A(A3), .B(B3), .T_in(subtratorc2_1_t_out), .S(out_12), .T_out(subtratorc1_1_t_out));
  Hex_Digit_Display hex_digit_display_1 (.value({out_12, out_11, out_10, out_9}));  // open: dp
  // also tied to GND on the sheet: subtratorc1_1_t_out
endmodule

module SubtratorC1 (
  input  A,
  input  B,
  input  T_in,
  output S,
  output T_out
);

  wire and_1_out, and_2_out, and_3_out, not_1_out, not_2_out, xor_1_out;

  xor xor_1 (xor_1_out, A, B);
  not not_1 (not_1_out, A);
  not not_2 (not_2_out, A);
  and and_1 (and_1_out, B, T_in);
  and and_2 (and_2_out, T_in, not_1_out);
  and and_3 (and_3_out, B, not_2_out);
  xor xor_2 (S, xor_1_out, T_in);
  or or_1 (T_out, and_1_out, and_2_out, and_3_out);
endmodule

module SubtratorC2 (
  input  A,
  input  B,
  input  T_in,
  output S,
  output T_out
);

  wire and_1_out, and_2_out, and_3_out, not_1_out, not_2_out, xor_1_out;

  xor xor_1 (xor_1_out, A, B);
  not not_1 (not_1_out, A);
  not not_2 (not_2_out, A);
  and and_1 (and_1_out, B, T_in);
  and and_2 (and_2_out, T_in, not_1_out);
  and and_3 (and_3_out, B, not_2_out);
  xor xor_2 (S, xor_1_out, T_in);
  or or_1 (T_out, and_1_out, and_2_out, and_3_out);
endmodule

module SubtratorC3 (
  input  A,
  input  B,
  input  T_in,
  output S,
  output T_out
);

  wire and_1_out, and_2_out, and_3_out, not_1_out, not_2_out, xor_1_out;

  xor xor_1 (xor_1_out, A, B);
  not not_1 (not_1_out, A);
  not not_2 (not_2_out, A);
  and and_1 (and_1_out, B, T_in);
  and and_2 (and_2_out, T_in, not_1_out);
  and and_3 (and_3_out, B, not_2_out);
  xor xor_2 (S, xor_1_out, T_in);
  or or_1 (T_out, and_1_out, and_2_out, and_3_out);
endmodule

module SubtratorH (
  input  A,
  input  B,
  output S,
  output T_out
);

  wire not_1_out;

  not not_1 (not_1_out, A);
  xor xor_1 (S, A, B);
  and and_1 (T_out, B, not_1_out);
endmodule

module Comparador (
  input  a3,
  input  b3,
  input  a2,
  input  b2,
  input  a1,
  input  b1,
  input  a0,
  input  b0,
  output AeqB,
  output AltB_A_B,
  output AgtB_A_B
);

  wire and_2_out, and_3_out, and_4_out, and_5_out, not_1_out, not_2_out, not_3_out, not_4_out, xnor_1_out,
       xnor_2_out, xnor_3_out, xnor_4_out;

  xnor xnor_1 (xnor_1_out, a3, b3);
  xnor xnor_2 (xnor_2_out, a2, b2);
  xnor xnor_3 (xnor_3_out, a1, b1);
  xnor xnor_4 (xnor_4_out, a0, b0);
  not not_1 (not_1_out, b3);
  not not_2 (not_2_out, b2);
  not not_3 (not_3_out, b1);
  not not_4 (not_4_out, b0);
  and and_1 (AeqB, xnor_1_out, xnor_2_out, xnor_3_out, xnor_4_out);
  and and_2 (and_2_out, not_1_out, a3);
  and and_3 (and_3_out, xnor_1_out, not_2_out, a2);
  and and_4 (and_4_out, xnor_1_out, xnor_2_out, not_3_out, a1);
  and and_5 (and_5_out, xnor_1_out, xnor_2_out, xnor_3_out, not_4_out, a0);
  or or_1 (AgtB_A_B, and_2_out, and_3_out, and_4_out, and_5_out);
  nor nor_1 (AltB_A_B, AeqB, AgtB_A_B);
endmodule

module SomadorH (
  input  A,
  input  B,
  output S,
  output C_out
);

  xor xor_1 (S, A, B);
  and and_1 (C_out, B, A);
endmodule

module SomadorF1 (
  input  A,
  input  B,
  input  Cin,
  output S,
  output C_out
);

  wire and_1_out, and_2_out, and_3_out, xor_1_out;

  xor xor_1 (xor_1_out, A, B);
  and and_1 (and_1_out, B, Cin);
  and and_2 (and_2_out, Cin, A);
  and and_3 (and_3_out, B, A);
  xor xor_2 (S, xor_1_out, Cin);
  or or_1 (C_out, and_1_out, and_2_out, and_3_out);
endmodule

module SomadorF2 (
  input  A,
  input  B,
  input  Cin,
  output S,
  output C_out
);

  wire and_1_out, and_2_out, and_3_out, xor_1_out;

  xor xor_1 (xor_1_out, A, B);
  and and_1 (and_1_out, B, Cin);
  and and_2 (and_2_out, Cin, A);
  and and_3 (and_3_out, B, A);
  xor xor_2 (S, xor_1_out, Cin);
  or or_1 (C_out, and_1_out, and_2_out, and_3_out);
endmodule

module SomadorF3 (
  input  A,
  input  B,
  input  Cin,
  output S,
  output C_out
);

  wire and_1_out, and_2_out, and_3_out, xor_1_out;

  xor xor_1 (xor_1_out, A, B);
  and and_1 (and_1_out, B, Cin);
  and and_2 (and_2_out, Cin, A);
  and and_3 (and_3_out, B, A);
  xor xor_2 (S, xor_1_out, Cin);
  or or_1 (C_out, and_1_out, and_2_out, and_3_out);
endmodule

module Somador (
  input  A0,
  input  A1,
  input  A2,
  input  A3,
  input  B0,
  input  B1,
  input  B2,
  input  B3,
  output out_9,
  output out_10,
  output out_11,
  output out_12
);

  wire somadorf1_1_c_out, somadorf2_1_c_out, somadorf3_1_c_out, somadorh_1_c_out;

  SomadorH somadorh_1 (.A(A3), .B(B3), .S(out_9), .C_out(somadorh_1_c_out));
  SomadorF1 somadorf1_1 (.A(A2), .B(B2), .Cin(somadorh_1_c_out), .S(out_10), .C_out(somadorf1_1_c_out));
  SomadorF2 somadorf2_1 (.A(A1), .B(B1), .Cin(somadorf1_1_c_out), .S(out_11), .C_out(somadorf2_1_c_out));
  SomadorF3 somadorf3_1 (.A(A0), .B(B0), .Cin(somadorf2_1_c_out), .S(out_12), .C_out(somadorf3_1_c_out));
  Hex_Digit_Display hex_digit_display_1 (.value({out_12, out_11, out_10, out_9}));  // open: dp
  // also tied to GND on the sheet: somadorf3_1_c_out
endmodule

module Multiplicador (
  input  A0,
  input  A1,
  input  A2,
  input  A3,
  input  B0,
  input  B1,
  input  B2,
  input  B3,
  output out_0
);

  and b0a0 (out_0, B0, A0);
  // AND_Gate b0a1 has open pins: in0=A1, in1=B0, out=open
  // AND_Gate b0a2 has open pins: in0=A2, in1=B0, out=open
  // AND_Gate b0a3 has open pins: in0=A3, in1=B0, out=open
  // AND_Gate b1a0 has open pins: in0=B1, in1=A0, out=open
  // AND_Gate b1a1 has open pins: in0=B1, in1=A1, out=open
  // AND_Gate b1a2 has open pins: in0=B1, in1=A2, out=open
  // AND_Gate b2a0 has open pins: in0=B2, in1=A0, out=open
  // AND_Gate b2a1 has open pins: in0=B2, in1=A1, out=open
  // AND_Gate b3a0 has open pins: in0=A0, in1=B3, out=open
endmodule

module Multiplexador (
  input  in_1,
  input  in_2,
  input  in_3,
  input  in_4,
  input  C1,
  input  C2,
  output S
);

  wire and_1_out, and_2_out, and_3_out, and_4_out, not_1_out, not_2_out, not_3_out, not_4_out, not_5_out,
       not_6_out;

  not not_1 (not_1_out, C1);
  not not_2 (not_2_out, C2);
  not not_3 (not_3_out, C1);
  not not_4 (not_4_out, C2);
  not not_5 (not_5_out, C1);
  not not_6 (not_6_out, C2);
  and and_1 (and_1_out, in_1, not_1_out, not_2_out);
  and and_2 (and_2_out, in_2, not_3_out, C2);
  and and_3 (and_3_out, in_3, C1, not_4_out);
  and and_4 (and_4_out, in_4, not_5_out, not_6_out);
  or or_1 (S, and_1_out, and_2_out, and_3_out, and_4_out);
endmodule

module Subtrator_Menor_Maior (
  input  A3,
  input  A2,
  input  A1,
  input  A0,
  input  B3,
  input  B2,
  input  B1,
  input  B0,
  output out_9,
  output out_10,
  output out_11,
  output out_12
);

  wire not_1_out, not_2_out, not_3_out, not_4_out, somadorh_1_c_out, somadorh_2_c_out, somadorh_3_c_out,
       somadorh_4_c_out, subtratorc1_1_s, subtratorc1_1_t_out, subtratorc2_1_s, subtratorc2_1_t_out,
       subtratorc3_1_s, subtratorc3_1_t_out, subtratorh_1_s, subtratorh_1_t_out;

  SubtratorH subtratorh_1 (.A(A0), .B(B0), .S(subtratorh_1_s), .T_out(subtratorh_1_t_out));
  SubtratorC3 subtratorc3_1 (
    .A(A1), .B(B1), .T_in(subtratorh_1_t_out), .S(subtratorc3_1_s), .T_out(subtratorc3_1_t_out));
  SubtratorC2 subtratorc2_1 (
    .A(A2), .B(B2), .T_in(subtratorc3_1_t_out), .S(subtratorc2_1_s), .T_out(subtratorc2_1_t_out));
  SubtratorC1 subtratorc1_1 (
    .A(A3), .B(B3), .T_in(subtratorc2_1_t_out), .S(subtratorc1_1_s), .T_out(subtratorc1_1_t_out));
  not not_1 (not_1_out, subtratorh_1_s);
  not not_2 (not_2_out, subtratorc3_1_s);
  not not_3 (not_3_out, subtratorc2_1_s);
  not not_4 (not_4_out, subtratorc1_1_s);
  SomadorH somadorh_1 (.A(1'b1), .B(not_1_out), .S(out_9), .C_out(somadorh_1_c_out));
  SomadorH somadorh_2 (.A(somadorh_1_c_out), .B(not_2_out), .S(out_10), .C_out(somadorh_2_c_out));
  SomadorH somadorh_3 (.A(somadorh_2_c_out), .B(not_3_out), .S(out_11), .C_out(somadorh_3_c_out));
  SomadorH somadorh_4 (.A(somadorh_3_c_out), .B(not_4_out), .S(out_12), .C_out(somadorh_4_c_out));
  Hex_Digit_Display hex_digit_display_1 (.value({out_12, out_11, out_10, out_9}));  // open: dp
  // also tied to GND on the sheet: {subtratorc1_1_t_out, somadorh_4_c_out}
endmodule

module Subtrator_Mestre (
  input  in_1,
  input  A,
  input  in_3,
  input  in_4,
  input  in_5,
  input  B,
  input  in_7,
  input  in_8
);

  wire comparador_1_altb_a_b, not_1_out, submestrecon_1_out_10, submestrecon_1_out_11, submestrecon_1_out_12,
       submestrecon_1_out_13, submestrecon_1_out_14, submestrecon_1_out_15, submestrecon_1_out_16,
       submestrecon_1_out_17, submestrecon_2_out_10, submestrecon_2_out_11, submestrecon_2_out_12,
       submestrecon_2_out_13, submestrecon_2_out_14, submestrecon_2_out_15, submestrecon_2_out_16,
       submestrecon_2_out_17;
  wire [3:0] subtrator_maior_menor_1_out_9, subtrator_menor_maior_1_out_9;

  Comparador comparador_1 (
    .a3(in_4), .b3(in_8), .a2(in_3), .b2(in_7), .a1(A), .b1(B), .a0(in_1), .b0(in_5),
    .AltB_A_B(comparador_1_altb_a_b));  // open: AeqB, AgtB_A_B
  SubMestreCon submestrecon_1 (
    .in_1(in_1), .in_2(A), .in_3(in_3), .in_4(in_4), .in_5(in_5), .in_6(B), .in_7(in_7), .in_8(in_8),
    .in_9(not_1_out), .out_10(submestrecon_1_out_10), .out_11(submestrecon_1_out_11),
    .out_12(submestrecon_1_out_12), .out_13(submestrecon_1_out_13), .out_14(submestrecon_1_out_14),
    .out_15(submestrecon_1_out_15), .out_16(submestrecon_1_out_16), .out_17(submestrecon_1_out_17));
  not not_1 (not_1_out, comparador_1_altb_a_b);
  SubMestreCon submestrecon_2 (
    .in_1(in_1), .in_2(A), .in_3(in_3), .in_4(in_4), .in_5(in_5), .in_6(B), .in_7(in_7), .in_8(in_8),
    .in_9(comparador_1_altb_a_b), .out_10(submestrecon_2_out_10), .out_11(submestrecon_2_out_11),
    .out_12(submestrecon_2_out_12), .out_13(submestrecon_2_out_13), .out_14(submestrecon_2_out_14),
    .out_15(submestrecon_2_out_15), .out_16(submestrecon_2_out_16), .out_17(submestrecon_2_out_17));
  Subtrator_Maior_Menor subtrator_maior_menor_1 (
    .A3(submestrecon_1_out_13), .A2(submestrecon_1_out_12), .A1(submestrecon_1_out_11),
    .A0(submestrecon_1_out_10), .B3(submestrecon_1_out_17), .B2(submestrecon_1_out_16),
    .B1(submestrecon_1_out_15), .B0(submestrecon_1_out_14), .out_9(subtrator_maior_menor_1_out_9[0]),
    .out_10(subtrator_maior_menor_1_out_9[1]), .out_11(subtrator_maior_menor_1_out_9[2]),
    .out_12(subtrator_maior_menor_1_out_9[3]));
  Subtrator_Menor_Maior subtrator_menor_maior_1 (
    .A3(submestrecon_2_out_13), .A2(submestrecon_2_out_12), .A1(submestrecon_2_out_11),
    .A0(submestrecon_2_out_10), .B3(submestrecon_2_out_17), .B2(submestrecon_2_out_16),
    .B1(submestrecon_2_out_15), .B0(submestrecon_2_out_14), .out_9(subtrator_menor_maior_1_out_9[0]),
    .out_10(subtrator_menor_maior_1_out_9[1]), .out_11(subtrator_menor_maior_1_out_9[2]),
    .out_12(subtrator_menor_maior_1_out_9[3]));
  Hex_Digit_Display hex_digit_display_1 (.value(subtrator_maior_menor_1_out_9));  // open: dp
  Hex_Digit_Display hex_digit_display_2 (.value(subtrator_menor_maior_1_out_9));  // open: dp
endmodule

module SubMestreCon (
  input  in_1,
  input  in_2,
  input  in_3,
  input  in_4,
  input  in_5,
  input  in_6,
  input  in_7,
  input  in_8,
  input  in_9,
  output out_10,
  output out_11,
  output out_12,
  output out_13,
  output out_14,
  output out_15,
  output out_16,
  output out_17
);

  and and_1 (out_10, in_1, in_9);
  and and_2 (out_11, in_2, in_9);
  and and_3 (out_12, in_3, in_9);
  and and_4 (out_13, in_4, in_9);
  and and_5 (out_14, in_5, in_9);
  and and_6 (out_15, in_6, in_9);
  and and_7 (out_16, in_7, in_9);
  and and_8 (out_17, in_8, in_9);
endmodule
